// Logisim project ex5-solution.circ as structural Verilog: 5 circuits, main circuit rotr
module rotr (
  input  [15:0] A,
  input  [3:0] B,
  output [15:0] Out1
);

  wire [15:0] multiplexer_1_out, multiplexer_2_out, multiplexer_3_out, rot1_1_out_2, rot2_1_out_2,
       rot4_1_out_2, rot8_1_out_2;

  rot1 rot1_1 (.in_1(A), .out_2(rot1_1_out_2));
  Multiplexer #(.width(16), .enable("false")) multiplexer_1 (
    .in0(A), .in1(rot1_1_out_2), .out(multiplexer_1_out), .sel(B[0]));
  Multiplexer #(.width(16), .enable("false")) multiplexer_2 (
    .in0(multiplexer_1_out), .in1(rot2_1_out_2), .out(multiplexer_2_out), .sel(B[1]));
  rot2 rot2_1 (.in_1(multiplexer_1_out), .out_2(rot2_1_out_2));
  rot4 rot4_1 (.in_1(multiplexer_2_out), .out_2(rot4_1_out_2));
  Multiplexer #(.width(16), .enable("false")) multiplexer_3 (
    .in0(multiplexer_2_out), .in1(rot4_1_out_2), .out(multiplexer_3_out), .sel(B[2]));
  rot8 rot8_1 (.in_1(multiplexer_3_out), .out_2(rot8_1_out_2));
  Multiplexer #(.width(16), .enable("false")) multiplexer_4 (
    .in0(multiplexer_3_out), .in1(rot8_1_out_2), .out(Out1), .sel(B[3]));

  // Notes on the sheet:
  //   PUT CIRCUITRY HERE
endmodule

module rot8 (
  input  [15:0] in_1,
  output [15:0] out_2
);


  assign out_2 = {in_1[7:0], in_1[15:8]};

  // Other names for the same wires on the sheet: input_8_15[7:0] = in_1[15:8]; input_0_7[7:0] = in_1[7:0]

  // Notes on the sheet:
  //   PUT CIRCUITRY HERE
endmodule

module rot4 (
  input  [15:0] in_1,
  output [15:0] out_2
);


  assign out_2 = {in_1[3:0], in_1[15:4]};

  // Other names for the same wires on the sheet: input_4_15[11:0] = in_1[15:4]; input_0_3[3:0] = in_1[3:0]

  // Notes on the sheet:
  //   PUT CIRCUITRY HERE
endmodule

module rot2 (
  input  [15:0] in_1,
  output [15:0] out_2
);


  assign out_2 = {in_1[1:0], in_1[15:2]};

  // Other names for the same wires on the sheet: input_2_15[13:0] = in_1[15:2]; input_0_1[1:0] = in_1[1:0]

  // Notes on the sheet:
  //   PUT CIRCUITRY HERE
endmodule

module rot1 (
  input  [15:0] in_1,
  output [15:0] out_2
);


  assign out_2 = {in_1[0], in_1[15:1]};

  // Other names for the same wires on the sheet: input_1_15[14:0] = in_1[15:1]; input_0 = in_1[0]

  // Notes on the sheet:
  //   PUT CIRCUITRY HERE
endmodule
