// Logisim project alu.circ as structural Verilog: 1 circuit, main circuit alu
module alu (
  input  [31:0] A,
  input  [31:0] B,
  input  [3:0] ALUSel,
  output [31:0] Result
);

  wire [0:0] slt7;
  wire [31:0] add0, and1, divu8, mul10, mulh14, mulhu11, multiplier_3_cout, multiplier_4_cout, neg_neg,
       neg_pos, negator_1_out, negator_2_out, or2, pos_neg, pos_pos, remu9, sll6, sra5, srl4, sub12, xor3;

  Negator #(.width(32)) negator_1 (.in(A), .out(negator_1_out));
  Negator #(.width(32)) negator_2 (.in(B), .out(negator_2_out));
  Multiplier #(.width(32)) multiplier_1 (.a(A), .b(B), .cout(pos_pos));  // open: out, cin
  Multiplier #(.width(32)) multiplier_2 (.a(negator_1_out), .b(negator_2_out), .cout(neg_neg));  // open: out, cin
  Multiplier #(.width(32)) multiplier_3 (.a(A), .b(B), .cout(multiplier_3_cout));  // open: out, cin
  Multiplier #(.width(32)) multiplier_4 (.a(A), .b(B), .cout(multiplier_4_cout));  // open: out, cin
  Subtractor #(.width(32)) subtractor_1 (.a(multiplier_3_cout), .b(B), .out(neg_pos));  // open: bin, bout
  Subtractor #(.width(32)) subtractor_2 (.a(multiplier_4_cout), .b(A), .out(pos_neg));  // open: bin, bout
  Adder #(.width(32)) adder_1 (.a(A), .b(B), .out(add0));  // open: cin, cout
  assign and1 = A & B;  // AND_Gate and_1, 32 bits wide
  assign or2 = A | B;  // OR_Gate or_1, 32 bits wide
  assign xor3 = A ^ B;  // XOR_Gate xor_1, 32 bits wide
  Shifter #(.width(32), .shift("lr")) shifter_1 (.in(A), .\dist (B[4:0]), .out(srl4));
  Shifter #(.width(32), .shift("ar")) shifter_2 (.in(A), .\dist (B[4:0]), .out(sra5));
  Shifter #(.width(32)) shifter_3 (.in(A), .\dist (B[4:0]), .out(sll6));
  Comparator #(.width(32)) comparator_1 (.a(A), .b(B), .lt(slt7[0]));  // open: gt, eq
  Divider #(.width(32)) divider_1 (.a(A), .b(B), .out(divu8), .rem(remu9));  // open: upper
  Multiplier #(.width(32)) multiplier_5 (.a(A), .b(B), .out(mul10), .cout(mulhu11));  // open: cin
  Subtractor #(.width(32)) subtractor_3 (.a(A), .b(B), .out(sub12));  // open: bin, bout
  Multiplexer #(.select(4), .width(32), .enable("false")) multiplexer_1 (
    .in0(add0), .in1(and1), .in2(or2), .in3(xor3), .in4(srl4), .in5(sra5), .in6(sll6),
    .in7({{31{1'b0}}, slt7[0]}), .in8(divu8), .in9(remu9), .in10(mul10), .in11(mulhu11), .in12(sub12),
    .in13(B), .in14(mulh14), .out(Result), .sel(ALUSel));  // open: in15
  Multiplexer #(.select(2), .width(32), .enable("false")) multiplexer_2 (
    .in0(pos_pos), .in1(neg_pos), .in2(pos_neg), .in3(neg_neg), .out(mulh14), .sel({B[31], A[31]}));

  // Other names for the same wires on the sheet: A_sign = A[31]; B_sign = B[31]; bsel13[31:0] = B;
  //   A_mag[30:0] = A[30:0]; B_mag[30:0] = B[30:0]

  // Notes on the sheet:
  //   INPUTS to your circuit
  //   DON'T CHANGE THE LOCATIONS OF THE INPUTS AND OUTPUTS!
  //   OUTPUT from your circuit
endmodule
