// Logisim project branch_comp.circ as structural Verilog: 1 circuit, main circuit branch_comp
module branch_comp (
  input  [31:0] rs1,
  input  [31:0] rs2,
  input  BrUn,
  output BrEq,
  output BrLt
);

  wire signedEq, signedLt, unsignedEq, unsignedLt;

  Comparator #(.width(32), .mode("unsigned")) comparator_1 (
    .a(rs1), .b(rs2), .eq(unsignedEq), .lt(unsignedLt));  // open: gt
  Comparator #(.width(32)) comparator_2 (.a(rs1), .b(rs2), .eq(signedEq), .lt(signedLt));  // open: gt
  Multiplexer #(.enable("false")) multiplexer_1 (.in0(signedEq), .in1(unsignedEq), .out(BrEq), .sel(BrUn));
  Multiplexer #(.enable("false")) multiplexer_2 (.in0(signedLt), .in1(unsignedLt), .out(BrLt), .sel(BrUn));

  // Notes on the sheet:
  //   INPUTS to your circuit
  //   DON'T CHANGE THE LOCATIONS OF THE INPUTS AND OUTPUTS!
  //   OUTPUT from your circuit
endmodule
