// Logisim project control_logic-solution.circ as structural Verilog: 12 circuits, main circuit PCSel_processor
module control_logic (
  input  [31:0] inst,
  input  BrEq,
  input  BrLt,
  output PCSel,
  output RegWEn,
  output [2:0] ImmSel,
  output BrUn,
  output ASel,
  output BSel,
  output [3:0] ALUSel,
  output MemRW,
  output [1:0] WBSel,
  output BrSel,
  output AddrSel
);

  PCSel_processor pcsel_processor_1 (.Opcode(inst[6:0]), .Funct3(inst[14:12]), .BrEq(BrEq), .BrLt(BrLt), .PCSel(PCSel));
  RegWEn_processor regwen_processor_1 (.Opcode(inst[6:0]), .RegWEn(RegWEn));
  ImmSel_processor immsel_processor_1 (.Opcode(inst[6:0]), .Funct3(inst[14:12]), .ImmSel(ImmSel));
  BrUn_processor brun_processor_1 (.Opcode(inst[6:0]), .Funct3(inst[14:12]), .BrUn(BrUn));
  ASel_processor asel_processor_1 (.Opcode(inst[6:0]), .ASel(ASel));
  BSel_processor bsel_processor_1 (.Opcode(inst[6:0]), .BSel(BSel));
  ALU_processor alu_processor_1 (.Opcode(inst[6:0]), .Funct3(inst[14:12]), .Funct7(inst[31:25]), .ALUSel(ALUSel));
  MemRW_processor memrw_processor_1 (.Opcode(inst[6:0]), .Funct3(inst[14:12]), .BrEq(BrEq), .BrLt(BrLt), .MemRW(MemRW));
  WBSel_processor wbsel_processor_1 (.Opcode(inst[6:0]), .Funct3(inst[14:12]), .WBSel(WBSel));
  BrSel_processor brsel_processor_1 (.Opcode(inst[6:0]), .Funct3(inst[14:12]), .BrSel(BrSel));
  AddrSel_processor addrsel_processor_1 (
    .Opcode(inst[6:0]), .Funct3(inst[14:12]), .BrEq(BrEq), .BrLt(BrLt), .AddrSel(AddrSel));

  // Other names for the same wires on the sheet: Opcode[6:0] = inst[6:0]; Funct3[2:0] = inst[14:12];
  //   Funct7[6:0] = inst[31:25]

  // Notes on the sheet:
  //   INPUTS to your circuit
  //   DON'T CHANGE THE LOCATIONS OF THE INPUTS AND OUTPUTS!
  //   OUTPUT from your circuit
endmodule

module PCSel_processor (
  input  [6:0] Opcode,
  input  [2:0] Funct3,
  input  BrEq,
  input  BrLt,
  output PCSel
);

  wire A, f000, f001, f100, f101, f110, f111, or_1_out;

  Multiplexer #(.select(2), .enable("false")) multiplexer_1 (
    .in0(1'b0), .in1(1'b0), .in2(1'b1), .out(f000), .sel({BrEq, BrLt}));  // open: in3
  Multiplexer #(.select(2), .enable("false")) multiplexer_2 (
    .in0(1'b1), .in1(1'b1), .in2(1'b0), .out(f001), .sel({BrEq, BrLt}));  // open: in3
  or or_1 (or_1_out, Opcode[2], A);
  and and_1 (PCSel, Opcode[6], or_1_out);
  Multiplexer #(.select(2), .enable("false")) multiplexer_3 (
    .in0(1'b0), .in1(1'b1), .in2(1'b0), .out(f100), .sel({BrEq, BrLt}));  // open: in3
  Multiplexer #(.select(2), .enable("false")) multiplexer_4 (
    .in0(1'b1), .in1(1'b0), .in2(1'b1), .out(f101), .sel({BrEq, BrLt}));  // open: in3
  Multiplexer #(.select(2), .enable("false")) multiplexer_5 (
    .in0(1'b0), .in1(1'b1), .in2(1'b0), .out(f110), .sel({BrEq, BrLt}));  // open: in3
  Multiplexer #(.select(2), .enable("false")) multiplexer_6 (
    .in0(1'b1), .in1(1'b0), .in2(1'b1), .out(f111), .sel({BrEq, BrLt}));  // open: in3
  Multiplexer #(.select(3), .enable("false")) multiplexer_7 (
    .in0(f000), .in1(f001), .in4(f100), .in5(f101), .in6(f110), .in7(f111), .out(A), .sel(Funct3));  // open: in2, in3

  // Other names for the same wires on the sheet: Br[1:0] = {BrEq, BrLt}

  // Notes on the sheet:
  //   INPUT
  //   OUTPUT
endmodule

module RegWEn_processor (
  input  [6:0] Opcode,
  output RegWEn
);

  wire and_1_out, not_1_out, not_2_out, not_3_out;

  not not_1 (not_1_out, Opcode[2]);
  not not_2 (not_2_out, Opcode[3]);
  not not_3 (not_3_out, Opcode[4]);
  and and_1 (and_1_out, not_1_out, not_2_out, not_3_out, Opcode[5]);
  not not_4 (RegWEn, and_1_out);

  // Notes on the sheet:
  //   INPUT
  //   OUTPUT
endmodule

module ImmSel_processor (
  input  [6:0] Opcode,
  input  [2:0] Funct3,
  output [2:0] ImmSel
);

  wire and_4_out, and_5_out, and_7_out, and_8_out, and_10_out, I000, IR101, not_1_out, not_2_out, not_3_out,
       not_4_out, not_5_out, not_6_out, not_7_out, not_8_out, not_9_out, not_10_out, not_11_out, not_12_out,
       not_13_out, not_14_out, not_15_out, not_16_out, not_17_out, not_18_out, not_19_out, not_20_out,
       not_21_out, not_22_out, not_23_out, S001, SB010, U011, UJ100;
  wire [2:0] bitfinder_1_index;

  not not_1 (not_1_out, Opcode[2]);
  not not_2 (not_2_out, Opcode[3]);
  not not_3 (not_3_out, Opcode[4]);
  not not_4 (not_4_out, Opcode[6]);
  not not_5 (not_5_out, Opcode[2]);
  not not_6 (not_6_out, Opcode[3]);
  not not_7 (not_7_out, Opcode[4]);
  not not_8 (not_8_out, Opcode[3]);
  not not_9 (not_9_out, Opcode[6]);
  and and_1 (S001, not_1_out, not_2_out, not_3_out, Opcode[5], not_4_out);
  and and_2 (SB010, not_5_out, not_6_out, not_7_out, Opcode[5], Opcode[6]);
  and and_3 (U011, Opcode[2], not_8_out, Opcode[4], not_9_out);
  BitFinder #(.width(6)) bitfinder_1 (
    .in({UJ100, U011, IR101, SB010, S001, I000}), .index(bitfinder_1_index));  // open: found
  not not_10 (not_10_out, Opcode[4]);
  not not_11 (not_11_out, Opcode[3]);
  not not_12 (not_12_out, Opcode[4]);
  not not_13 (not_13_out, Opcode[2]);
  not not_14 (not_14_out, Opcode[3]);
  not not_15 (not_15_out, Opcode[4]);
  not not_16 (not_16_out, Opcode[5]);
  not not_17 (not_17_out, Opcode[6]);
  not not_18 (not_18_out, Opcode[2]);
  not not_19 (not_19_out, Opcode[3]);
  not not_20 (not_20_out, Opcode[5]);
  not not_21 (not_21_out, Opcode[6]);
  not not_22 (not_22_out, Funct3[1]);
  and and_4 (and_4_out, not_18_out, not_19_out, not_20_out, not_21_out);
  and and_5 (and_5_out, Funct3[0], not_22_out);
  Multiplexer #(.select(3), .width(3), .enable("false")) multiplexer_1 (
    .in0(3'b000), .in1(3'b001), .in2(3'b010), .in3(3'b101), .in4(3'b011), .in5(3'b100), .out(ImmSel),
    .sel(bitfinder_1_index));  // open: in6, in7
  and and_6 (UJ100, Opcode[2], Opcode[3], not_10_out, Opcode[5], Opcode[6]);
  and and_7 (and_7_out, Opcode[2], not_11_out, not_12_out, Opcode[5], Opcode[6]);
  and and_8 (and_8_out, not_13_out, not_14_out, not_15_out, not_16_out, not_17_out);
  and and_9 (IR101, and_4_out, and_5_out);
  not not_23 (not_23_out, IR101);
  and and_10 (and_10_out, and_4_out, not_23_out);
  or or_1 (I000, and_7_out, and_8_out, and_10_out);

  // Notes on the sheet:
  //   INPUT
  //   OUTPUT
endmodule

module BrUn_processor (
  input  [6:0] Opcode,
  input  [2:0] Funct3,
  output BrUn
);

  wire not_1_out, not_2_out, not_3_out;

  not not_1 (not_1_out, Opcode[2]);
  not not_2 (not_2_out, Opcode[3]);
  not not_3 (not_3_out, Opcode[4]);
  and and_1 (BrUn, not_1_out, not_2_out, not_3_out, Opcode[5], Opcode[6], Funct3[1], Funct3[2]);

  // Notes on the sheet:
  //   INPUT
  //   OUTPUT
endmodule

module ASel_processor (
  input  [6:0] Opcode,
  output ASel
);

  wire not_1_out, not_2_out, not_3_out, not_4_out, not_5_out, not_6_out, SB, U, UJ;

  not not_1 (not_1_out, Opcode[2]);
  not not_2 (not_2_out, Opcode[3]);
  not not_3 (not_3_out, Opcode[4]);
  not not_4 (not_4_out, Opcode[3]);
  not not_5 (not_5_out, Opcode[6]);
  not not_6 (not_6_out, Opcode[4]);
  and and_1 (SB, not_1_out, not_2_out, not_3_out, Opcode[5], Opcode[6]);
  and and_2 (U, Opcode[2], not_4_out, Opcode[4], not_5_out);
  and and_3 (UJ, Opcode[2], Opcode[3], not_6_out, Opcode[5], Opcode[6]);
  or or_1 (ASel, SB, U, UJ);

  // Notes on the sheet:
  //   INPUT
  //   OUTPUT
endmodule

module BSel_processor (
  input  [6:0] Opcode,
  output BSel
);

  wire and_1_out, not_1_out, not_2_out, not_3_out;

  not not_1 (not_1_out, Opcode[2]);
  not not_2 (not_2_out, Opcode[3]);
  not not_3 (not_3_out, Opcode[6]);
  and and_1 (and_1_out, not_1_out, not_2_out, Opcode[4], Opcode[5], not_3_out);
  not not_4 (BSel, and_1_out);

  // Notes on the sheet:
  //   INPUT
  //   OUTPUT
endmodule

module ALU_processor (
  input  [6:0] Opcode,
  input  [2:0] Funct3,
  input  [6:0] Funct7,
  output [3:0] ALUSel
);

  wire and_3_out, and_4_out, and_13_out, and_14_out, and_15_out, and_16_out, and_17_out, and_23_out,
       and_24_out, and_25_out, and_26_out, and_27_out, and_28_out, and_34_out, and_35_out, and_36_out,
       and_37_out, and_38_out, and_39_out, I0000, II0000, IR0000, Is_IR, Is_R, not_1_out, not_2_out,
       not_3_out, not_4_out, not_5_out, not_6_out, not_7_out, not_8_out, not_9_out, not_10_out, not_11_out,
       not_12_out, not_13_out, not_14_out, not_15_out, not_16_out, not_17_out, not_18_out, not_19_out,
       not_20_out, not_21_out, not_22_out, not_23_out, not_24_out, not_25_out, not_26_out, not_27_out,
       not_28_out, not_29_out, not_30_out, not_31_out, not_32_out, not_33_out, not_34_out, not_35_out,
       not_36_out, not_37_out, not_38_out, not_39_out, not_40_out, not_41_out, not_42_out, not_43_out,
       not_44_out, not_45_out, not_46_out, not_47_out, not_48_out, not_49_out, not_50_out, not_51_out,
       not_52_out, not_53_out, not_54_out, not_55_out, or_2_out, or_3_out, or_4_out, or_5_out, or_6_out,
       or_7_out, OUT0000, OUT0001, OUT0010, OUT0011, OUT0100, OUT0101, OUT0110, OUT0111, OUT1000, OUT1001,
       OUT1010, OUT1011, OUT1100, OUT1110, R0000, S0000, SB0000, U0000, UJ0000;
  wire [3:0] bitfinder_1_index;

  not not_1 (not_1_out, Opcode[2]);
  not not_2 (not_2_out, Opcode[3]);
  not not_3 (not_3_out, Opcode[4]);
  not not_4 (not_4_out, Opcode[4]);
  not not_5 (not_5_out, Opcode[3]);
  not not_6 (not_6_out, Opcode[6]);
  not not_7 (not_7_out, Opcode[3]);
  not not_8 (not_8_out, Opcode[4]);
  not not_9 (not_9_out, Funct3[0]);
  not not_10 (not_10_out, Funct3[1]);
  not not_11 (not_11_out, Funct3[2]);
  not not_12 (not_12_out, Funct7[0]);
  not not_13 (not_13_out, Funct7[5]);
  not not_14 (not_14_out, Funct3[0]);
  not not_15 (not_15_out, Funct3[1]);
  not not_16 (not_16_out, Funct3[2]);
  and and_1 (SB0000, not_1_out, not_2_out, not_3_out, Opcode[5], Opcode[6]);
  and and_2 (UJ0000, Opcode[2], Opcode[3], not_4_out, Opcode[5], Opcode[6]);
  and and_3 (and_3_out, not_9_out, not_10_out, not_11_out);
  and and_4 (and_4_out, not_14_out, not_15_out, not_16_out);
  and and_5 (U0000, Opcode[2], not_5_out, Opcode[4], not_6_out);
  and and_6 (I0000, Opcode[2], not_7_out, not_8_out, Opcode[5], Opcode[6]);
  and and_7 (IR0000, Is_IR, and_3_out);
  and and_8 (R0000, Is_R, not_12_out, not_13_out, and_4_out);
  not not_17 (not_17_out, Opcode[2]);
  not not_18 (not_18_out, Opcode[3]);
  not not_19 (not_19_out, Opcode[4]);
  not not_20 (not_20_out, Opcode[6]);
  not not_21 (not_21_out, Opcode[2]);
  not not_22 (not_22_out, Opcode[3]);
  not not_23 (not_23_out, Opcode[4]);
  not not_24 (not_24_out, Opcode[5]);
  not not_25 (not_25_out, Opcode[6]);
  not not_26 (not_26_out, Opcode[2]);
  not not_27 (not_27_out, Opcode[3]);
  not not_28 (not_28_out, Opcode[5]);
  not not_29 (not_29_out, Opcode[6]);
  not not_30 (not_30_out, Opcode[2]);
  not not_31 (not_31_out, Opcode[3]);
  not not_32 (not_32_out, Opcode[6]);
  or or_1 (OUT0000, SB0000, UJ0000, U0000, I0000, IR0000, R0000, S0000, II0000);
  and and_9 (S0000, not_17_out, not_18_out, not_19_out, Opcode[5], not_20_out);
  and and_10 (II0000, not_21_out, not_22_out, not_23_out, not_24_out, not_25_out);
  and and_11 (Is_IR, not_26_out, not_27_out, Opcode[4], not_28_out, not_29_out);
  and and_12 (Is_R, not_30_out, not_31_out, Opcode[4], Opcode[5], not_32_out);
  not not_33 (not_33_out, Funct3[0]);
  not not_34 (not_34_out, Funct3[1]);
  not not_35 (not_35_out, Funct7[0]);
  not not_36 (not_36_out, Funct3[1]);
  not not_37 (not_37_out, Funct3[2]);
  not not_38 (not_38_out, Funct3[0]);
  not not_39 (not_39_out, Funct3[2]);
  not not_40 (not_40_out, Funct3[0]);
  not not_41 (not_41_out, Funct3[1]);
  not not_42 (not_42_out, Funct3[2]);
  not not_43 (not_43_out, Funct3[0]);
  not not_44 (not_44_out, Funct3[1]);
  not not_45 (not_45_out, Funct3[2]);
  or or_2 (or_2_out, Is_IR, Is_R);
  and and_13 (and_13_out, not_33_out, not_34_out, Funct3[2]);
  or or_3 (or_3_out, Is_IR, Is_R);
  and and_14 (and_14_out, Funct3[0], not_36_out, not_37_out);
  or or_4 (or_4_out, Is_IR, Is_R);
  and and_15 (and_15_out, not_38_out, Funct3[1], not_39_out);
  and and_16 (and_16_out, not_40_out, not_41_out, not_42_out);
  and and_17 (and_17_out, not_43_out, not_44_out, not_45_out);
  and and_18 (OUT0011, or_2_out, and_13_out);
  and and_19 (OUT0110, or_3_out, not_35_out, and_14_out);
  and and_20 (OUT0111, or_4_out, and_15_out);
  and and_21 (OUT1100, Is_R, Funct7[5], and_16_out);
  and and_22 (OUT1010, Is_R, Funct7[0], and_17_out);
  not not_46 (not_46_out, Funct3[0]);
  not not_47 (not_47_out, Funct7[5]);
  not not_48 (not_48_out, Funct7[0]);
  not not_49 (not_49_out, Funct3[1]);
  not not_50 (not_50_out, Funct3[1]);
  not not_51 (not_51_out, Funct3[1]);
  not not_52 (not_52_out, Funct3[2]);
  not not_53 (not_53_out, Funct3[1]);
  or or_5 (or_5_out, Is_IR, Is_R);
  and and_23 (and_23_out, not_46_out, Funct3[1], Funct3[2]);
  or or_6 (or_6_out, Is_IR, Is_R);
  and and_24 (and_24_out, not_47_out, not_48_out);
  and and_25 (and_25_out, Funct3[0], not_49_out, Funct3[2]);
  or or_7 (or_7_out, Is_IR, Is_R);
  and and_26 (and_26_out, Funct3[0], not_50_out, Funct3[2]);
  and and_27 (and_27_out, Funct3[0], not_51_out, not_52_out);
  and and_28 (and_28_out, Funct3[0], not_53_out, Funct3[2]);
  and and_29 (OUT0010, or_5_out, and_23_out);
  and and_30 (OUT0100, or_6_out, and_24_out, and_25_out);
  and and_31 (OUT0101, or_7_out, Funct7[5], and_26_out);
  and and_32 (OUT1110, Is_R, Funct7[0], and_27_out);
  and and_33 (OUT1000, Is_R, Funct7[0], and_28_out);
  and and_34 (and_34_out, Funct3[0], Funct3[1], Funct3[2]);
  not not_54 (not_54_out, Funct7[0]);
  not not_55 (not_55_out, Funct3[2]);
  and and_35 (and_35_out, Funct3[0], Funct3[1], Funct3[2]);
  and and_36 (and_36_out, Funct3[0], Funct3[1], not_55_out);
  and and_37 (and_37_out, Funct3[0], Funct3[1], Funct3[2]);
  and and_38 (and_38_out, Is_IR, and_34_out);
  and and_39 (and_39_out, Is_R, not_54_out, and_35_out);
  and and_40 (OUT1011, Is_R, Funct7[0], and_36_out);
  and and_41 (OUT1001, Is_R, Funct7[0], and_37_out);
  or or_8 (OUT0001, and_38_out, and_39_out);
  BitFinder #(.width(14)) bitfinder_1 (
    .in({OUT1110, OUT1100, OUT1011, OUT1010, OUT1001, OUT1000, OUT0111, OUT0110, OUT0101, OUT0100, OUT0011, OUT0010, OUT0001, OUT0000}),
    .index(bitfinder_1_index));  // open: found
  Multiplexer #(.select(4), .width(4), .enable("false")) multiplexer_1 (
    .in0(4'b0000), .in1(4'b0001), .in2(4'b0010), .in3(4'b0011), .in4(4'b0100), .in5(4'b0101), .in6(4'b0110),
    .in7(4'b0111), .in8(4'b1000), .in9(4'b1001), .in10(4'b1010), .in11(4'b1011), .in12(4'b1100),
    .in13(4'b1110), .out(ALUSel), .sel(bitfinder_1_index));  // open: in14, in15

  // Notes on the sheet:
  //   INPUT
  //   OUTPUT
endmodule

module MemRW_processor (
  input  [6:0] Opcode,
  input  [2:0] Funct3,
  input  BrEq,
  input  BrLt,
  output MemRW
);

  wire and_2_out, and_3_out, is_S, not_1_out, not_2_out, not_3_out, not_4_out, not_5_out, not_6_out,
       not_7_out, or_1_out;

  not not_1 (not_1_out, Opcode[2]);
  not not_2 (not_2_out, Opcode[3]);
  not not_3 (not_3_out, Opcode[4]);
  not not_4 (not_4_out, Opcode[6]);
  and and_1 (is_S, not_1_out, not_2_out, not_3_out, Opcode[5], not_4_out);
  not not_5 (not_5_out, BrEq);
  not not_6 (not_6_out, Funct3[0]);
  not not_7 (not_7_out, Funct3[2]);
  and and_2 (and_2_out, not_6_out, Funct3[1], not_7_out);
  and and_3 (and_3_out, Funct3[0], Funct3[1], Funct3[2], not_5_out, BrLt);
  or or_1 (or_1_out, and_2_out, and_3_out);
  and and_4 (MemRW, is_S, or_1_out);

  // Notes on the sheet:
  //   INPUT
  //   OUTPUT
endmodule

module WBSel_processor (
  input  [6:0] Opcode,
  input  [2:0] Funct3,
  output [1:0] WBSel
);

  wire is_I10, Is_IR, Is_R, Is_U01, is_UJ, not_1_out, not_2_out, not_3_out, not_4_out, not_5_out, not_6_out,
       not_7_out, not_8_out, not_9_out, not_10_out, not_11_out, not_12_out, not_13_out, not_14_out,
       not_15_out, not_16_out, not_17_out, not_18_out, not_19_out, not_20_out, OUT00, OUT01, OUT10, OUT11;
  wire [1:0] bitfinder_1_index;

  not not_1 (not_1_out, Opcode[2]);
  not not_2 (not_2_out, Opcode[3]);
  not not_3 (not_3_out, Opcode[6]);
  not not_4 (not_4_out, Opcode[2]);
  not not_5 (not_5_out, Opcode[3]);
  not not_6 (not_6_out, Opcode[5]);
  not not_7 (not_7_out, Opcode[6]);
  not not_8 (not_8_out, Opcode[3]);
  not not_9 (not_9_out, Opcode[5]);
  not not_10 (not_10_out, Opcode[6]);
  not not_11 (not_11_out, Opcode[3]);
  not not_12 (not_12_out, Opcode[4]);
  not not_13 (not_13_out, Opcode[4]);
  and and_1 (Is_R, not_1_out, not_2_out, Opcode[4], Opcode[5], not_3_out);
  and and_2 (Is_IR, not_4_out, not_5_out, Opcode[4], not_6_out, not_7_out);
  and and_3 (Is_U01, Opcode[2], not_8_out, Opcode[4], not_9_out, not_10_out);
  and and_4 (is_UJ, Opcode[2], Opcode[3], not_13_out, Opcode[5], Opcode[6]);
  and and_5 (is_I10, Opcode[2], not_11_out, not_12_out, Opcode[5], Opcode[6]);
  not not_14 (not_14_out, Opcode[2]);
  not not_15 (not_15_out, Opcode[3]);
  not not_16 (not_16_out, Opcode[4]);
  not not_17 (not_17_out, Opcode[5]);
  not not_18 (not_18_out, Opcode[6]);
  not not_19 (not_19_out, Opcode[3]);
  not not_20 (not_20_out, Opcode[6]);
  or or_1 (OUT10, is_UJ, is_I10);
  or or_2 (OUT01, Is_R, Is_U01, Is_IR);
  and and_6 (OUT00, not_14_out, not_15_out, not_16_out, not_17_out, not_18_out);
  and and_7 (OUT11, Opcode[2], not_19_out, Opcode[4], Opcode[5], not_20_out);
  BitFinder #(.width(4)) bitfinder_1 (.in({OUT11, OUT10, OUT01, OUT00}), .index(bitfinder_1_index));  // open: found
  Multiplexer #(.select(2), .width(2), .enable("false")) multiplexer_1 (
    .in0(2'b00), .in1(2'b01), .in2(2'b10), .in3(2'b11), .out(WBSel), .sel(bitfinder_1_index));

  // Notes on the sheet:
  //   INPUT
  //   OUTPUT
endmodule

module BrSel_processor (
  input  [6:0] Opcode,
  input  [2:0] Funct3,
  output BrSel
);

  wire not_1_out, not_2_out, not_3_out, not_4_out;

  not not_1 (not_1_out, Opcode[2]);
  not not_2 (not_2_out, Opcode[3]);
  not not_3 (not_3_out, Opcode[4]);
  not not_4 (not_4_out, Opcode[6]);
  and and_1 (BrSel, not_1_out, not_2_out, not_3_out, Opcode[5], not_4_out);

  // Notes on the sheet:
  //   INPUT
  //   OUTPUT
endmodule

module AddrSel_processor (
  input  [6:0] Opcode,
  input  [2:0] Funct3,
  input  BrEq,
  input  BrLt,
  output AddrSel
);

  wire not_1_out, not_2_out, not_3_out, not_4_out, not_5_out;

  not not_1 (not_1_out, Opcode[2]);
  not not_2 (not_2_out, Opcode[3]);
  not not_3 (not_3_out, Opcode[4]);
  not not_4 (not_4_out, Opcode[6]);
  not not_5 (not_5_out, BrEq);
  and and_1 (AddrSel, not_1_out, not_2_out, not_3_out, Opcode[5], not_4_out, Funct3[0], Funct3[0], Funct3[0], not_5_out, BrLt);

  // Notes on the sheet:
  //   INPUT
  //   OUTPUT
endmodule
