// Logisim project control_logic.circ as structural Verilog: 1 circuit, main circuit control_logic
module control_logic (
  input  [31:0] inst,
  input  BrEq,
  input  BrLt,
  output PCSel,
  output RegWEn,
  output [2:0] ImmSel,
  output BrUn,
  output ASel,
  output BSel,
  output [3:0] ALUSel,
  output MemRW,
  output [1:0] WBSel
);

  wire and_34_out, and_35_out, and_36_out, and_37_out, and_38_out, and_39_out, comparator_10_eq,
       comparator_11_eq, comparator_12_eq, comparator_13_eq, comparator_14_eq, comparator_15_eq,
       comparator_16_eq, comparator_17_eq, comparator_18_eq, comparator_19_eq, comparator_20_eq,
       comparator_21_eq, comparator_22_eq, comparator_23_eq, comparator_24_eq, comparator_25_eq,
       comparator_26_eq, comparator_27_eq, comparator_28_eq, comparator_29_eq, comparator_30_eq,
       comparator_31_eq, comparator_32_eq, comparator_33_eq, comparator_34_eq, comparator_35_eq,
       comparator_36_eq, comparator_37_eq, comparator_38_eq, comparator_39_eq, comparator_40_eq,
       comparator_41_eq, comparator_42_eq, comparator_43_eq, comparator_44_eq, comparator_45_eq,
       comparator_46_eq, comparator_47_eq, comparator_48_eq, comparator_49_eq, comparator_50_eq,
       comparator_51_eq, comparator_52_eq, comparator_53_eq, comparator_54_eq, comparator_55_eq,
       comparator_56_eq, comparator_57_eq, comparator_58_eq, comparator_59_eq, is_add, is_addi, is_and,
       is_andi, is_beq, is_bge, is_bgeu, is_blt, is_bltu, is_bne, is_divu, is_lb, is_lh, is_lw, is_mul,
       is_mulh, is_mulhu, is_or, is_ori, is_remu, is_sll, is_slli, is_slt, is_slti, is_sra, is_srai, is_srl,
       is_srli, is_sub, is_sw, is_swlt, is_xor, is_xori, isI_jalr, isI_load, isI_norm, isR, isS, isSB,
       isU_auipc, isU_lui, isUJ_jal, not_1_out, not_2_out, not_3_out, or_1_out, or_5_out, or_10_out,
       or_11_out, or_12_out, or_13_out, or_15_out, or_17_out, or_19_out, or_20_out, or_22_out, or_23_out,
       or_24_out, or_25_out, or_26_out, or_34_out, or_35_out, or_36_out;
  wire [1:0] bitfinder_2_index;
  wire [2:0] bitfinder_3_index;
  wire [3:0] bitfinder_1_index, or_29_out, or_38_out;
  wire [7:0] or_2_out;

  Comparator #(.width(7)) comparator_1 (.a(inst[6:0]), .b(7'b0110011), .eq(isR));  // open: gt, lt
  Comparator #(.width(7)) comparator_2 (.a(inst[6:0]), .b(7'b0000011), .eq(isI_load));  // open: gt, lt
  Comparator #(.width(7)) comparator_3 (.a(inst[6:0]), .b(7'b0010011), .eq(isI_norm));  // open: gt, lt
  Comparator #(.width(7)) comparator_4 (.a(inst[6:0]), .b(7'b0100011), .eq(isS));  // open: gt, lt
  Comparator #(.width(7)) comparator_5 (.a(inst[6:0]), .b(7'b1100011), .eq(isSB));  // open: gt, lt
  Comparator #(.width(7)) comparator_6 (.a(inst[6:0]), .b(7'b0010111), .eq(isU_auipc));  // open: gt, lt
  Comparator #(.width(7)) comparator_7 (.a(inst[6:0]), .b(7'b0110111), .eq(isU_lui));  // open: gt, lt
  Comparator #(.width(7)) comparator_8 (.a(inst[6:0]), .b(7'b1101111), .eq(isUJ_jal));  // open: gt, lt
  Comparator #(.width(7)) comparator_9 (.a(inst[6:0]), .b(7'b1100111), .eq(isI_jalr));  // open: gt, lt
  Comparator #(.width(3)) comparator_10 (.a(inst[14:12]), .b(3'b001), .eq(comparator_10_eq));  // open: gt, lt
  Comparator #(.width(7)) comparator_11 (.a(inst[31:25]), .b(7'b0000001), .eq(comparator_11_eq));  // open: gt, lt
  Comparator #(.width(3)) comparator_12 (.a(inst[14:12]), .b(3'b011), .eq(comparator_12_eq));  // open: gt, lt
  Comparator #(.width(7)) comparator_13 (.a(inst[31:25]), .b(7'b0000001), .eq(comparator_13_eq));  // open: gt, lt
  Comparator #(.width(3)) comparator_14 (.a(inst[14:12]), .b(3'b110), .eq(comparator_14_eq));  // open: gt, lt
  Comparator #(.width(7)) comparator_15 (.a(inst[31:25]), .b({7{1'b0}}), .eq(comparator_15_eq));  // open: gt, lt
  Comparator #(.width(3)) comparator_16 (.a(inst[14:12]), .b(3'b111), .eq(comparator_16_eq));  // open: gt, lt
  Comparator #(.width(7)) comparator_17 (.a(inst[31:25]), .b(7'b0000001), .eq(comparator_17_eq));  // open: gt, lt
  Comparator #(.width(3)) comparator_18 (.a(inst[14:12]), .b(3'b111), .eq(comparator_18_eq));  // open: gt, lt
  Comparator #(.width(7)) comparator_19 (.a(inst[31:25]), .b({7{1'b0}}), .eq(comparator_19_eq));  // open: gt, lt
  Comparator #(.width(3)) comparator_20 (.a(inst[14:12]), .b(3'b000), .eq(comparator_20_eq));  // open: gt, lt
  Comparator #(.width(7)) comparator_21 (.a(inst[31:25]), .b({7{1'b0}}), .eq(comparator_21_eq));  // open: gt, lt
  Comparator #(.width(3)) comparator_22 (.a(inst[14:12]), .b(3'b000), .eq(comparator_22_eq));  // open: gt, lt
  Comparator #(.width(7)) comparator_23 (.a(inst[31:25]), .b(7'b0000001), .eq(comparator_23_eq));  // open: gt, lt
  Comparator #(.width(3)) comparator_24 (.a(inst[14:12]), .b(3'b000), .eq(comparator_24_eq));  // open: gt, lt
  Comparator #(.width(7)) comparator_25 (.a(inst[31:25]), .b(7'b0100000), .eq(comparator_25_eq));  // open: gt, lt
  Comparator #(.width(3)) comparator_26 (.a(inst[14:12]), .b(3'b001), .eq(comparator_26_eq));  // open: gt, lt
  Comparator #(.width(7)) comparator_27 (.a(inst[31:25]), .b({7{1'b0}}), .eq(comparator_27_eq));  // open: gt, lt
  Comparator #(.width(3)) comparator_28 (.a(inst[14:12]), .b(3'b010), .eq(comparator_28_eq));  // open: gt, lt
  Comparator #(.width(7)) comparator_29 (.a(inst[31:25]), .b({7{1'b0}}), .eq(comparator_29_eq));  // open: gt, lt
  Comparator #(.width(3)) comparator_30 (.a(inst[14:12]), .b(3'b100), .eq(comparator_30_eq));  // open: gt, lt
  Comparator #(.width(7)) comparator_31 (.a(inst[31:25]), .b({7{1'b0}}), .eq(comparator_31_eq));  // open: gt, lt
  Comparator #(.width(3)) comparator_32 (.a(inst[14:12]), .b(3'b101), .eq(comparator_32_eq));  // open: gt, lt
  Comparator #(.width(7)) comparator_33 (.a(inst[31:25]), .b(7'b0000001), .eq(comparator_33_eq));  // open: gt, lt
  Comparator #(.width(3)) comparator_34 (.a(inst[14:12]), .b(3'b101), .eq(comparator_34_eq));  // open: gt, lt
  Comparator #(.width(7)) comparator_35 (.a(inst[31:25]), .b({7{1'b0}}), .eq(comparator_35_eq));  // open: gt, lt
  Comparator #(.width(3)) comparator_36 (.a(inst[14:12]), .b(3'b101), .eq(comparator_36_eq));  // open: gt, lt
  Comparator #(.width(7)) comparator_37 (.a(inst[31:25]), .b(7'b0100000), .eq(comparator_37_eq));  // open: gt, lt
  and and_1 (is_add, isR, comparator_20_eq, comparator_21_eq);
  and and_2 (is_mul, isR, comparator_22_eq, comparator_23_eq);
  and and_3 (is_sub, isR, comparator_24_eq, comparator_25_eq);
  and and_4 (is_sll, isR, comparator_26_eq, comparator_27_eq);
  and and_5 (is_mulh, isR, comparator_10_eq, comparator_11_eq);
  and and_6 (is_mulhu, isR, comparator_12_eq, comparator_13_eq);
  and and_7 (is_slt, isR, comparator_28_eq, comparator_29_eq);
  and and_8 (is_xor, isR, comparator_30_eq, comparator_31_eq);
  and and_9 (is_divu, isR, comparator_32_eq, comparator_33_eq);
  and and_10 (is_srl, isR, comparator_34_eq, comparator_35_eq);
  and and_11 (is_sra, isR, comparator_36_eq, comparator_37_eq);
  and and_12 (is_or, isR, comparator_14_eq, comparator_15_eq);
  and and_13 (is_remu, isR, comparator_16_eq, comparator_17_eq);
  and and_14 (is_and, isR, comparator_18_eq, comparator_19_eq);
  Comparator #(.width(3)) comparator_38 (.a(inst[14:12]), .b(3'b000), .eq(comparator_38_eq));  // open: gt, lt
  Comparator #(.width(3)) comparator_39 (.a(inst[14:12]), .b(3'b001), .eq(comparator_39_eq));  // open: gt, lt
  Comparator #(.width(7)) comparator_40 (.a(inst[31:25]), .b({7{1'b0}}), .eq(comparator_40_eq));  // open: gt, lt
  Comparator #(.width(3)) comparator_41 (.a(inst[14:12]), .b(3'b010), .eq(comparator_41_eq));  // open: gt, lt
  Comparator #(.width(3)) comparator_42 (.a(inst[14:12]), .b(3'b100), .eq(comparator_42_eq));  // open: gt, lt
  Comparator #(.width(3)) comparator_43 (.a(inst[14:12]), .b(3'b101), .eq(comparator_43_eq));  // open: gt, lt
  Comparator #(.width(7)) comparator_44 (.a(inst[31:25]), .b({7{1'b0}}), .eq(comparator_44_eq));  // open: gt, lt
  Comparator #(.width(3)) comparator_45 (.a(inst[14:12]), .b(3'b101), .eq(comparator_45_eq));  // open: gt, lt
  Comparator #(.width(7)) comparator_46 (.a(inst[31:25]), .b(7'b0100000), .eq(comparator_46_eq));  // open: gt, lt
  Comparator #(.width(3)) comparator_47 (.a(inst[14:12]), .b(3'b111), .eq(comparator_47_eq));  // open: gt, lt
  Comparator #(.width(3)) comparator_48 (.a(inst[14:12]), .b(3'b010), .eq(comparator_48_eq));  // open: gt, lt
  Comparator #(.width(3)) comparator_49 (.a(inst[14:12]), .b(3'b111), .eq(comparator_49_eq));  // open: gt, lt
  Comparator #(.width(3)) comparator_50 (.a(inst[14:12]), .b(3'b000), .eq(comparator_50_eq));  // open: gt, lt
  Comparator #(.width(3)) comparator_51 (.a(inst[14:12]), .b(3'b001), .eq(comparator_51_eq));  // open: gt, lt
  Comparator #(.width(3)) comparator_52 (.a(inst[14:12]), .b(3'b010), .eq(comparator_52_eq));  // open: gt, lt
  Comparator #(.width(3)) comparator_53 (.a(inst[14:12]), .b(3'b110), .eq(comparator_53_eq));  // open: gt, lt
  and and_15 (is_lb, isI_load, comparator_50_eq);
  and and_16 (is_lh, isI_load, comparator_51_eq);
  and and_17 (is_lw, isI_load, comparator_52_eq);
  and and_18 (is_addi, isI_norm, comparator_38_eq);
  and and_19 (is_slli, isI_norm, comparator_39_eq, comparator_40_eq);
  and and_20 (is_slti, isI_norm, comparator_41_eq);
  and and_21 (is_xori, isI_norm, comparator_42_eq);
  and and_22 (is_srli, isI_norm, comparator_43_eq, comparator_44_eq);
  and and_23 (is_srai, isI_norm, comparator_45_eq, comparator_46_eq);
  and and_24 (is_ori, isI_norm, comparator_53_eq);
  and and_25 (is_andi, isI_norm, comparator_47_eq);
  and and_26 (is_sw, isS, comparator_48_eq);
  and and_27 (is_swlt, isS, comparator_49_eq);
  Comparator #(.width(3)) comparator_54 (.a(inst[14:12]), .b(3'b000), .eq(comparator_54_eq));  // open: gt, lt
  Comparator #(.width(3)) comparator_55 (.a(inst[14:12]), .b(3'b001), .eq(comparator_55_eq));  // open: gt, lt
  Comparator #(.width(3)) comparator_56 (.a(inst[14:12]), .b(3'b100), .eq(comparator_56_eq));  // open: gt, lt
  Comparator #(.width(3)) comparator_57 (.a(inst[14:12]), .b(3'b101), .eq(comparator_57_eq));  // open: gt, lt
  Comparator #(.width(3)) comparator_58 (.a(inst[14:12]), .b(3'b110), .eq(comparator_58_eq));  // open: gt, lt
  Comparator #(.width(3)) comparator_59 (.a(inst[14:12]), .b(3'b111), .eq(comparator_59_eq));  // open: gt, lt
  and and_28 (is_beq, isSB, comparator_54_eq);
  and and_29 (is_bne, isSB, comparator_55_eq);
  and and_30 (is_blt, isSB, comparator_56_eq);
  and and_31 (is_bge, isSB, comparator_57_eq);
  and and_32 (is_bltu, isSB, comparator_58_eq);
  and and_33 (is_bgeu, isSB, comparator_59_eq);
  or or_1 (or_1_out, is_beq, is_bne, is_blt, is_bge, is_bltu, is_bgeu);
  or or_2 (or_2_out[0], or_1_out, is_add, is_lb, is_lh, is_lw, is_addi, is_sw, isU_auipc, isUJ_jal, isI_jalr);
  or or_3 (or_2_out[4], is_srl, is_srli);
  or or_4 (or_2_out[5], is_sra, is_srai);
  or or_5 (or_5_out, is_lb, is_lh, is_lw);
  or or_6 (or_2_out[2], is_or, is_ori);
  or or_7 (or_2_out[3], is_xor, is_xori);
  or or_8 (or_2_out[6], is_slli, is_sll);
  or or_9 (or_2_out[7], is_slti, is_slt);
  or or_10 (or_10_out, is_beq, is_bne, is_blt, is_bge, is_bltu, is_bgeu);
  or or_11 (or_11_out, isU_auipc, isUJ_jal);
  or or_12 (or_12_out, is_mul, is_divu, is_sub, is_remu, is_and, is_or, is_add, is_addi, is_sll, is_mulh, is_mulhu, is_slt, is_srl, is_xor, is_sra);
  or or_13 (or_13_out, or_5_out, isI_jalr, isU_auipc, isUJ_jal);
  or or_14 (or_2_out[1], is_and, is_andi);
  or or_15 (or_15_out, is_addi, is_slli, is_slti, is_xori, is_srli, is_srai, is_ori, is_andi);
  or or_16 (ASel, or_10_out, or_11_out);
  or or_17 (or_17_out, or_15_out, or_13_out);
  or or_18 (RegWEn, or_12_out, isU_lui, or_17_out);
  not not_1 (not_1_out, BrEq);
  not not_2 (not_2_out, BrLt);
  not not_3 (not_3_out, BrLt);
  and and_34 (and_34_out, is_beq, BrEq);
  and and_35 (and_35_out, is_bne, not_1_out);
  and and_36 (and_36_out, is_blt, BrLt);
  and and_37 (and_37_out, is_bge, not_2_out);
  and and_38 (and_38_out, is_bltu, BrLt);
  and and_39 (and_39_out, is_bgeu, not_3_out);
  BitFinder #(.width(15)) bitfinder_1 (
    .in({is_mulh, isU_lui, is_sub, is_mulhu, is_mul, is_remu, is_divu, or_2_out}), .index(bitfinder_1_index));  // open: found
  Multiplexer #(.select(4), .width(4), .enable("false")) multiplexer_1 (
    .in0(4'b0000), .in1(4'b0001), .in2(4'b0010), .in3(4'b0011), .in4(4'b0100), .in5(4'b0101), .in6(4'b0110),
    .in7(4'b0111), .in8(4'b1000), .in9(4'b1001), .in10(4'b1010), .in11(4'b1011), .in12(4'b1100),
    .in13(4'b1101), .in14(4'b1110), .out(ALUSel), .sel(bitfinder_1_index));  // open: in15
  or or_19 (or_19_out, is_beq, is_bne, is_blt, is_bge, is_bltu, is_bgeu);
  or or_20 (or_20_out, isI_jalr, isU_auipc, isU_lui, isUJ_jal);
  or or_21 (PCSel, and_34_out, and_35_out, and_36_out, and_37_out, and_38_out, and_39_out, isU_auipc, isUJ_jal, isI_jalr);
  or or_22 (or_22_out, is_sw, is_lb, is_lh, is_lw);
  or or_23 (or_23_out, is_addi, is_slli, is_slti, is_xori, is_srli, is_srai, is_ori, is_andi);
  or or_24 (or_24_out, is_mul, is_divu, is_sub, is_remu, is_and, is_or, is_add, is_addi, is_sll, is_mulh, is_mulhu, isU_auipc, is_slt, is_srl, is_xor, is_sra);
  or or_25 (or_25_out, is_addi, is_slli, is_slti, is_xori, is_srli, is_srai, is_ori, is_andi);
  or or_26 (or_26_out, or_22_out, or_23_out, or_19_out);
  or or_27 (or_29_out[1], or_24_out, isU_lui);
  or or_28 (BSel, or_26_out, or_20_out);
  or or_29 (or_29_out[0], is_lb, is_lh, is_lw);
  or or_30 (or_29_out[2], isUJ_jal, isI_jalr);
  BitFinder #(.width(4)) bitfinder_2 (.in(or_29_out), .index(bitfinder_2_index));  // open: found
  or or_31 (BrUn, is_bltu, is_bgeu);
  Multiplexer #(.select(2), .width(2), .enable("false")) multiplexer_2 (
    .in0(2'b00), .in1(2'b01), .in2(2'b10), .out(WBSel), .sel(bitfinder_2_index));  // open: in3
  or or_32 (or_38_out[2], is_beq, is_bne, is_blt, is_bge, is_bltu, is_bgeu);
  buf or_33 (MemRW, is_sw);  // OR_Gate
  or or_34 (or_34_out, is_lb, is_lh, is_lw);
  or or_35 (or_35_out, isI_jalr, or_34_out);
  or or_36 (or_36_out, is_addi, is_slli, is_slti, is_xori, is_srli, is_srai, is_ori, is_andi);
  or or_37 (or_38_out[3], isU_auipc, isU_lui);
  or or_38 (or_38_out[0], or_35_out, or_36_out);
  BitFinder #(.width(5)) bitfinder_3 (
    .in({isUJ_jal, or_38_out[3:2], is_sw, or_38_out[0]}), .index(bitfinder_3_index));  // open: found
  Multiplexer #(.select(3), .width(3), .enable("false")) multiplexer_3 (
    .in0(3'b000), .in1(3'b001), .in2(3'b010), .in3(3'b011), .in4(3'b100), .out(ImmSel),
    .sel(bitfinder_3_index));  // open: in5, in6, in7

  // Other names for the same wires on the sheet: Opcode[6:0] = inst[6:0]; funct3[2:0] = inst[14:12];
  //   funct7[6:0] = inst[31:25]

  // Notes on the sheet:
  //   INPUTS to your circuit
  //   DON'T CHANGE THE LOCATIONS OF THE INPUTS AND OUTPUTS!
  //   OUTPUT from your circuit
  //   R type instructions
  //   I type instruction
  //   S type instruction
  //   SB type instruction
endmodule
