// Logisim project cpu.circ as structural Verilog: 2 circuits, main circuit Process_mem_data
module main (
  input  [31:0] INSTRUCTION,
  input  CLOCK,
  output [31:0] PROGRAM_COUNTER,
  output [31:0] ra,
  output [31:0] sp,
  output [31:0] t0,
  output [31:0] t1,
  output [31:0] t2,
  output [31:0] s0,
  output [31:0] s1,
  output [31:0] a0
);

  wire ASel, BrEq, BrLT, BrUn, BSel, comparator_2_eq, comparator_3_eq, comparator_4_eq, is_lb, is_lh, is_lw,
       isI_load, MemRW, PCSel, RegWEn;
  wire [1:0] bitfinder_1_index, TypeSel, WBSel;
  wire [2:0] funct3, ImmSel;
  wire [3:0] ALUSel;
  wire [6:0] funct7;
  wire [24:0] INSTRUCTION_1;
  wire [31:0] ALU_Result, IMMEDIATE, MEM_READ_DATA, multiplexer_1_out, multiplexer_2_out, multiplexer_4_out,
       multiplexer_5_out, PC_plus4, PC_value, PC_value_plus4, RealMemData, rs1_data, rs2_data, WRITEBACK_DATA;

  control_logic control_logic_1 (
    .BSel(BSel), .RegWEn(RegWEn), .ASel(ASel), .ImmSel(ImmSel), .BrUn(BrUn), .PCSel(PCSel), .BrLt(BrLT),
    .BrEq(BrEq), .inst({funct7, INSTRUCTION_1[24:15], funct3, INSTRUCTION_1[11:0]}), .ALUSel(ALUSel),
    .MemRW(MemRW), .WBSel(WBSel));
  Register #(.width(32)) register_1 (
    .D(multiplexer_1_out), .clk(CLOCK), .Q({funct7, INSTRUCTION_1[24:15], funct3, INSTRUCTION_1[11:0]}));  // open: en, clr
  Multiplexer #(.width(32), .enable("false")) multiplexer_1 (
    .in0(INSTRUCTION), .in1(32'h13), .out(multiplexer_1_out), .sel(PCSel));
  imm_gen imm_gen_1 (
    .ImmSel(ImmSel), .imm(IMMEDIATE), .inst({funct7, INSTRUCTION_1[24:15], funct3, INSTRUCTION_1[11:0]}));
  Adder #(.width(32)) adder_1 (.a(PROGRAM_COUNTER), .b(32'h4), .out(PC_plus4));  // open: cin, cout
  Comparator #(.width(7)) comparator_1 (.a(INSTRUCTION_1[6:0]), .b(7'b0000011), .eq(isI_load));  // open: gt, lt
  Multiplexer #(.width(32), .enable("false")) multiplexer_2 (
    .in0(PC_plus4), .in1(ALU_Result), .out(multiplexer_2_out), .sel(PCSel));
  Register #(.width(32)) PC (.D(multiplexer_2_out), .clk(CLOCK), .Q(PROGRAM_COUNTER));  // open: en, clr
  Register #(.width(32)) register_2 (.D(PROGRAM_COUNTER), .clk(CLOCK), .Q(PC_value));  // open: en, clr
  Adder #(.width(32)) adder_2 (.a(PC_value), .b(32'h4), .out(PC_value_plus4));  // open: cin, cout
  Comparator #(.width(3)) comparator_2 (.a(funct3), .b(3'b000), .eq(comparator_2_eq));  // open: gt, lt
  Comparator #(.width(3)) comparator_3 (.a(funct3), .b(3'b001), .eq(comparator_3_eq));  // open: gt, lt
  Comparator #(.width(3)) comparator_4 (.a(funct3), .b(3'b010), .eq(comparator_4_eq));  // open: gt, lt
  and and_1 (is_lb, isI_load, comparator_2_eq);
  and and_2 (is_lh, isI_load, comparator_3_eq);
  and and_3 (is_lw, isI_load, comparator_4_eq);
  BitFinder #(.width(3)) bitfinder_1 (.in({is_lw, is_lh, is_lb}), .index(bitfinder_1_index));  // open: found
  Multiplexer #(.select(2), .width(2), .enable("false")) multiplexer_3 (
    .in0(2'b00), .in1(2'b01), .in2(2'b10), .out(TypeSel), .sel(bitfinder_1_index));  // open: in3
  regfile_main RegFile (
    .rs2(INSTRUCTION_1[24:20]), .rd(INSTRUCTION_1[11:7]), .Read_Data_1(rs1_data), .Read_Data_2(rs2_data),
    .ra(ra), .sp(sp), .t0(t0), .t1(t1), .t2(t2), .s0(s0), .s1(s1), .a0(a0), .rs1(INSTRUCTION_1[19:15]),
    .Write_Data(WRITEBACK_DATA), .RegWEn(RegWEn), .clk(CLOCK));
  branch_comp branch_comp_1 (.BrEq(BrEq), .BrUn(BrUn), .rs1(rs1_data), .BrLt(BrLT), .rs2(rs2_data));
  Multiplexer #(.width(32), .enable("false")) multiplexer_4 (
    .in0(rs1_data), .in1(PC_value), .out(multiplexer_4_out), .sel(ASel));
  Multiplexer #(.width(32), .enable("false")) multiplexer_5 (
    .in0(rs2_data), .in1(IMMEDIATE), .out(multiplexer_5_out), .sel(BSel));
  alu Arithmetic_Logic_Unit (.ALUSel(ALUSel), .Result(ALU_Result), .A(multiplexer_4_out), .B(multiplexer_5_out));
  // mem_main DMEM: pin names not known; wires that end beside it: ALU_Result, rs2_data, CLOCK, MemRW, MEM_READ_DATA
  Process_mem_data process_mem_data_1 (
    .TypeSel(TypeSel), .readInMemData(MEM_READ_DATA), .Address(ALU_Result), .processed_data(RealMemData));
  Multiplexer #(.select(2), .width(32), .enable("false")) multiplexer_6 (
    .in0(RealMemData), .in1(ALU_Result), .in2(PC_value_plus4), .out(WRITEBACK_DATA), .sel(WBSel));  // open: in3

  // Other names for the same wires on the sheet: clk = CLOCK; Opcode[6:0] = INSTRUCTION_1[6:0];
  //   opcode_t[6:0] = INSTRUCTION_1[6:0]; rd[4:0] = INSTRUCTION_1[11:7]; INSTRUCTION_1 (some bits) = {funct7, funct3};
  //   rs1[4:0] = INSTRUCTION_1[19:15]; rs2[4:0] = INSTRUCTION_1[24:20]

  // Notes on the sheet:
  //   Output
  //   IMEM (do **NOT** move this)
  //   Inputs
  //   It is OK to move the PC, RegFile, ALU, MEM, Branch Comp, Imm Gen, and Control Logic to wherever is most convenient for you when constructing your CPU, and to delete this text
  //   Inputs/Outputs for testing. Do **NOT** move these.
endmodule

module Process_mem_data (
  input  [1:0] TypeSel,
  input  [31:0] readInMemData,
  input  [31:0] Address,
  output [31:0] processed_data
);

  wire [31:0] lb_output, lh_output;
  wire [31:8] Byte0;

  assign Byte0 = {{23{readInMemData[7]}}, readInMemData[7]};  // Bit_Extender bit_extender_1
  Multiplexer #(.select(2), .width(32), .enable("false")) multiplexer_1 (
    .in0({Byte0, readInMemData[7:0]}), .in1({{25{readInMemData[15]}}, readInMemData[14:8]}),
    .in2({{25{readInMemData[23]}}, readInMemData[22:16]}),
    .in3({{25{readInMemData[31]}}, readInMemData[30:24]}), .out(lb_output), .sel(Address[1:0]));
  Multiplexer #(.width(32), .enable("false")) multiplexer_2 (
    .in0({{17{readInMemData[15]}}, readInMemData[14:0]}),
    .in1({{17{readInMemData[31]}}, readInMemData[30:16]}), .out(lh_output), .sel(Address[1]));
  Multiplexer #(.select(2), .width(32), .enable("false")) multiplexer_3 (
    .in0(lb_output), .in1(lh_output), .in2(readInMemData), .out(processed_data), .sel(TypeSel));  // open: in3

  // Other names for the same wires on the sheet: Addr[31:0] = Address; Byte0[7:0] = readInMemData[7:0];
  //   Half0[31:0] = {{17{readInMemData[15]}}, readInMemData[14:0]}; lw_output[31:0] = readInMemData;
  //   memData[31:0] = readInMemData; Byte1[31:0] = {{25{readInMemData[15]}}, readInMemData[14:8]};
  //   Byte2[31:0] = {{25{readInMemData[23]}}, readInMemData[22:16]};
  //   Half1[31:0] = {{17{readInMemData[31]}}, readInMemData[30:16]};
  //   Byte3[31:0] = {{25{readInMemData[31]}}, readInMemData[30:24]}; realOutput[31:0] = processed_data

  // Notes on the sheet:
  //   input
  //   output
endmodule
