// Logisim project imm_gen.circ as structural Verilog: 1 circuit, main circuit imm_gen
module imm_gen (
  input  [31:0] inst,
  input  [2:0] ImmSel,
  output [31:0] imm
);

  wire [31:12] I_imm, S_imm;
  wire [31:13] SB_imm;

  assign I_imm = {{19{inst[31]}}, inst[31]};  // Bit_Extender bit_extender_1
  assign S_imm = {{19{inst[31]}}, inst[31]};  // Bit_Extender bit_extender_2
  assign SB_imm = {{18{inst[31]}}, inst[31]};  // Bit_Extender bit_extender_3
  Multiplexer #(.select(3), .width(32), .enable("false")) multiplexer_1 (
    .in0({I_imm, inst[31:20]}), .in1({S_imm, inst[31:25], inst[11:7]}),
    .in2({SB_imm, inst[31], inst[7], inst[30:25], inst[11:8], 1'b0}), .in3({inst[31:12], {12{1'b0}}}),
    .in4({{12{inst[31]}}, inst[19:12], inst[20], inst[30:21], 1'b0}), .out(imm), .sel(ImmSel));  // open: in5, in6, in7

  // Other names for the same wires on the sheet: I_imm[11:0] = inst[31:20]; imm31to12[19:0] = inst[31:12];
  //   U_imm[31:12] = inst[31:12]; UJ_imm[31:1] = {{12{inst[31]}}, inst[19:12], inst[20], inst[30:21]};
  //   imm0to4[4:0] = inst[11:7]; imm4to1[3:0] = inst[11:8]; S_imm[11:0] = {inst[31:25], inst[11:7]};
  //   SB_imm[12:1] = {inst[31], inst[7], inst[30:25], inst[11:8]}; imm5to11[6:0] = inst[31:25];
  //   imm10to5[5:0] = inst[30:25]; imm11 = inst[7]; imm12 = inst[31]

  // Notes on the sheet:
  //   INPUTS to your circuit
  //   DON'T CHANGE THE LOCATIONS OF THE INPUTS AND OUTPUTS!
  //   OUTPUT from your circuit
endmodule
